# Fritzing sketch letterbox (saved by Fritzing 0.9.0b)
breadboards: 1

parts:
  Part1 = Arduino Uno (Rev3) - ICSP
  R1 = Photocell (LDR) [package=THT]
  R2 = Photocell (LDR) [package=THT]
  R3 = Resistor [package="2512 [SMD]"]
  R4 = Resistor [package="2512 [SMD]"]
  U1 = VCNL4000 [package=vcnl4000]
  RF1 = nRF8001 Bluetooth LE Breakout

nets:
  N1: Part1.A4/SDA, U1.SDA
  N2: Part1.A5/SCL, U1.SCL
  N3: Part1.ICSP_MISO, Part1.D12/MISO, RF1.MISO
  N4: Part1.ICSP_MOSI, Part1.D11_PWM/MOSI, RF1.MOSI
  N5: Part1.D9_PWM, RF1.RST
  N6: Part1.D10_PWM/SS, RF1.REQ
  N7: Part1.D13/SCK, RF1.SCK
  GND: Part1.GND, R3.Pin_0, R4.Pin_0, U1.GND
  N8: Part1.D2, RF1.RDY
  5V: Part1.5V, R1.pin_0, R2.pin_1, U1.VDD
  N9: R1.pin_1, R3.Pin_1
  N10: R2.pin_0, R4.Pin_1

notes:
  Postman LDR
  Owner
  LDR

custom parts:
  nRF8001 Bluetooth LE Breakout: nRF8001 Breakout Board
